# Fritzing sketch IOT_Fritzing (saved by Fritzing 0.9.3b)
breadboards: 2

parts:
  U1 = ESP32-38PinWide [part_number=ESP32-38PinWide]
  T1 = LM35 Temperature Sensor [package="TO92 [THT]"]
  R1 = Photocell (LDR) [package=THT]
  J1 = Basic Servo
  KY-1 = Keyes Relay [package=THT]
  R2 = Resistor [tolerance=±5% resistance=10 package="0603 [SMD]"]
  R4 = Resistor [tolerance=±5% resistance=220 package="0603 [SMD]"]
  VCC1 = 4 x AAA Battery Mount
  LED1 = LED - 3mm [color="Red (633nm)" package="3 mm [THT]"]
  T2 = LM35 Temperature Sensor [package="TO92 [THT]"]

nets:
  N1: U1.3.3, KY-1.power
  N2: U1.GPIO12, T2.Vout
  GND: U1.GND, T1.GND, J1.gnd, KY-1.ground, R2.Pin_1, R4.Pin_1, VCC1.-, T2.GND
  N3: U1.GPIO9, T1.Vout
  N4: U1.GPIO8, R1.pin_1, R2.Pin_0
  N5: U1.GPIO15, J1.pulse
  N6: U1.GPIO17, KY-1.signal
  N7: T1.+Vs, R1.pin_0, J1.vcc, KY-1.C, VCC1.+, T2.+Vs
  N8: KY-1.NO, LED1.cathode
  N9: R4.Pin_0, LED1.anode

custom parts:
  ESP32-38PinWide: Generic 38-Pin ESP32 with wide format (only access to one side of pins on a breadboard) based on Stephen Lilley's HiLetgo ESP-WROOM-32 ESP32 ESP-32S Development Board.
  Keyes Relay: The Keyes 5V relay module is suitable for SCM development, home appliance control. It uses a 5V~12V TIL control signal which can control DC / AC signal.
